# Fritzing sketch BuzzerCallerBluetooth (saved by Fritzing 0.9.4)
circuit board: 8.59691cm x 6.59163cm
breadboards: 1

parts:
  LED = smd LED [color="Red (633nm)" package="0805 [SMD]"]
  J1 = Piezo Speaker
  ESP-32 = ESP-WROOM-32 [ESP-32S] Module [part_number=ESP-WROOM-32]
  R1 = Resistor [tolerance=±5% resistance=220 package=THT]

nets:
  N1: LED.cathode, ESP-32.GND
  N2: LED.anode, R1.Pin_0
  N3: J1.pin1, J1.pin2, ESP-32.IO13
  N4: ESP-32.IO12, R1.Pin_1

notes:
  LED: IO 0
  PIEZO: IO 15

custom parts:
  ESP-WROOM-32 [ESP-32S] Module: Espressif ESP-WROOM-32 WiFi/Bluetooth LE microcontroller module also known as the Ai-Thinker ESP-32S module with similar formfactor. The ESP32 is a microcontroller chip with WiFi and BLE capabilities. The chip is developed by Espressif and is the successor to the popular ESP8266 WiFi module.

// code stored in the sketch: Untitled2.ino
#include <Config.h>
#include <EasyBuzzer.h>
const int buzzer = 15;
#define BLYNK_PRINT Serial
#include <WiFi.h>
#include <WiFiClient.h>
#include <BlynkSimpleEsp32.h>
int period = 500;
char auth[] = "AUTHKEY";
int led = 0;
char ssid[] = "SSID";
char pass[] = "PASS";
int freq = 2000;
int channel = 0;
int resolution = 8;

unsigned long time_now = 0;
void Alarm(){
       ledcWriteTone(channel, freq);
     time_now = millis();
     while(millis() < time_now + period){
        //wait approx. [period] ms
  
}
  ledcWriteTone(channel, freq+500);
     time_now = millis();
     while(millis() < time_now + period){
        //wait approx. [period] ms
  
}
  ledcWriteTone(channel, freq+1000);
     time_now = millis();
     while(millis() < time_now + period){
        //wait approx. [period] ms
  
}
  ledcWriteTone(channel, freq+1500);
     time_now = millis();
     while(millis() < time_now + period){
        //wait approx. [period] ms
  
}
  ledcWriteTone(channel, freq+2000);
     time_now = millis();
     while(millis() < time_now + period){
        //wait approx. [period] ms
  
}
}
BLYNK_WRITE(V1)
{
  int pinValue = param.asInt(); // assigning incoming value from pin V1 to a variable
  if(pinValue==1){
    
    digitalWrite(led,HIGH);
    Alarm();
    
  }
  else{
    digitalWrite(led,LOW);
     ledcWriteTone(channel, 0);
 
}
}
void setup()
{
  pinMode(led,OUTPUT);
  // Debug console
  Serial.begin(9600);
 
    ledcSetup(channel, freq, resolution);
  ledcAttachPin(15, channel);
  Blynk.begin(auth, ssid, pass);
  
  
}
void loop()
{
  Blynk.run();
}
